// Digital circuit adição.dig as structural Verilog
module \adição  (
  input  A0,
  input  B0,
  input  A1,
  input  B1,
  input  A2,
  input  B2,
  input  A3,
  input  B3,
  input  A4,
  input  B4,
  input  A5,
  input  B5,
  input  A6,
  input  B6,
  input  A7,
  input  B7,
  output S0,
  output S1,
  output S2,
  output S3,
  output S4,
  output S5,
  output S6,
  output S7,
  output S8
);

  wire \meioadição_1_co , \totaladição_2_co , \totaladição_3_co , \totaladição_4_co , \totaladição_5_co ,
       \totaladição_6_co , \totaladição_7_co ;

  \totaladição  \totaladição_1  (.A(A7), .B(B7), .Ci(\totaladição_2_co ), .S(S7), .Co(S8));
  \totaladição  \totaladição_2  (.A(A6), .B(B6), .Ci(\totaladição_3_co ), .S(S6), .Co(\totaladição_2_co ));
  \totaladição  \totaladição_3  (.A(A5), .B(B5), .Ci(\totaladição_4_co ), .S(S5), .Co(\totaladição_3_co ));
  \totaladição  \totaladição_4  (.A(A4), .B(B4), .Ci(\totaladição_5_co ), .S(S4), .Co(\totaladição_4_co ));
  \totaladição  \totaladição_5  (.A(A3), .B(B3), .Ci(\totaladição_6_co ), .S(S3), .Co(\totaladição_5_co ));
  \totaladição  \totaladição_6  (.A(A2), .B(B2), .Ci(\totaladição_7_co ), .S(S2), .Co(\totaladição_6_co ));
  \totaladição  \totaladição_7  (.A(A1), .B(B1), .Ci(\meioadição_1_co ), .S(S1), .Co(\totaladição_7_co ));
  \meioadição  \meioadição_1  (.A(A0), .B(B0), .S(S0), .Co(\meioadição_1_co ));
endmodule
