// Digital circuit comparador.dig as structural Verilog
module comparador (
  input  A0,
  input  B0,
  input  A1,
  input  A2,
  input  A3,
  input  A4,
  input  A5,
  input  A6,
  input  A7,
  input  B1,
  input  B2,
  input  B3,
  input  B4,
  input  B5,
  input  B6,
  input  B7,
  output O__lt,
  output O__eq,
  output O__gt
);

  wire meiocomparador_1_o__eq, meiocomparador_1_o__gt, meiocomparador_1_o__lt, totalcomparador_2_o__eq,
       totalcomparador_2_o__gt, totalcomparador_2_o__lt, totalcomparador_3_o__eq, totalcomparador_3_o__gt,
       totalcomparador_3_o__lt, totalcomparador_4_o__eq, totalcomparador_4_o__gt, totalcomparador_4_o__lt,
       totalcomparador_5_o__eq, totalcomparador_5_o__gt, totalcomparador_5_o__lt, totalcomparador_6_o__eq,
       totalcomparador_6_o__gt, totalcomparador_6_o__lt, totalcomparador_7_o__eq, totalcomparador_7_o__gt,
       totalcomparador_7_o__lt;

  totalcomparador totalcomparador_1 (
    .A(A7), .B(B7), .I_lt(totalcomparador_2_o__lt), .I_eq(totalcomparador_2_o__eq),
    .I_gt(totalcomparador_2_o__gt), .O__lt(O__lt), .O__eq(O__eq), .O__gt(O__gt));
  totalcomparador totalcomparador_2 (
    .A(A6), .B(B6), .I_lt(totalcomparador_3_o__lt), .I_eq(totalcomparador_3_o__eq),
    .I_gt(totalcomparador_3_o__gt), .O__lt(totalcomparador_2_o__lt), .O__eq(totalcomparador_2_o__eq),
    .O__gt(totalcomparador_2_o__gt));
  totalcomparador totalcomparador_3 (
    .A(A5), .B(B5), .I_lt(totalcomparador_4_o__lt), .I_eq(totalcomparador_4_o__eq),
    .I_gt(totalcomparador_4_o__gt), .O__lt(totalcomparador_3_o__lt), .O__eq(totalcomparador_3_o__eq),
    .O__gt(totalcomparador_3_o__gt));
  totalcomparador totalcomparador_4 (
    .A(A4), .B(B4), .I_lt(totalcomparador_5_o__lt), .I_eq(totalcomparador_5_o__eq),
    .I_gt(totalcomparador_5_o__gt), .O__lt(totalcomparador_4_o__lt), .O__eq(totalcomparador_4_o__eq),
    .O__gt(totalcomparador_4_o__gt));
  totalcomparador totalcomparador_5 (
    .A(A3), .B(B3), .I_lt(totalcomparador_6_o__lt), .I_eq(totalcomparador_6_o__eq),
    .I_gt(totalcomparador_6_o__gt), .O__lt(totalcomparador_5_o__lt), .O__eq(totalcomparador_5_o__eq),
    .O__gt(totalcomparador_5_o__gt));
  totalcomparador totalcomparador_6 (
    .A(A2), .B(B2), .I_lt(totalcomparador_7_o__lt), .I_eq(totalcomparador_7_o__eq),
    .I_gt(totalcomparador_7_o__gt), .O__lt(totalcomparador_6_o__lt), .O__eq(totalcomparador_6_o__eq),
    .O__gt(totalcomparador_6_o__gt));
  totalcomparador totalcomparador_7 (
    .A(A1), .B(B1), .I_lt(meiocomparador_1_o__lt), .I_eq(meiocomparador_1_o__eq),
    .I_gt(meiocomparador_1_o__gt), .O__lt(totalcomparador_7_o__lt), .O__eq(totalcomparador_7_o__eq),
    .O__gt(totalcomparador_7_o__gt));
  meiocomparador meiocomparador_1 (
    .A(A0), .B(B0), .O__lt(meiocomparador_1_o__lt), .O__eq(meiocomparador_1_o__eq),
    .O__gt(meiocomparador_1_o__gt));
endmodule
