// Digital circuit meiasubtração.dig as structural Verilog
module \meiasubtração  (
  input  A,
  input  B,
  output S,
  output Co
);

  xor xor_1 (S, A, B);
  and and_1 (Co, ~A, B);  // And
endmodule
