// Digital circuit multiplicador.dig as structural Verilog
module multiplicador (
  input  A0,
  input  A1,
  input  A2,
  input  A3,
  input  B0,
  input  B1,
  input  B2,
  input  B3,
  output S0,
  output S1,
  output S2,
  output S3,
  output S4,
  output S5,
  output S6,
  output S7
);

  wire \adição_1_s1 , \adição_1_s2 , \adição_1_s3 , \adição_1_s4 , \adição_1_s5 , \adição_2_s1 ,
       \adição_2_s2 , \adição_2_s3 , \adição_2_s4 , and_2_out, and_3_out, and_4_out, and_5_out, and_6_out,
       and_7_out, and_8_out, and_9_out, and_10_out, and_11_out, and_12_out, and_13_out, and_14_out,
       and_15_out, and_16_out;

  and and_1 (S0, A0, B0);
  and and_2 (and_2_out, A1, B0);
  and and_3 (and_3_out, A2, B0);
  and and_4 (and_4_out, A3, B0);
  and and_5 (and_5_out, A0, B1);
  and and_6 (and_6_out, A1, B1);
  and and_7 (and_7_out, A2, B1);
  and and_8 (and_8_out, A3, B1);
  \adição  \adição_1  (
    .A0(and_2_out), .B0(and_5_out), .A1(and_3_out), .B1(and_6_out), .A2(and_4_out), .B2(and_7_out),
    .A3(and_8_out), .B3(\adição_1_s5 ), .A4(\adição_1_s5 ), .B4(\adição_1_s5 ), .A5(\adição_1_s5 ),
    .B5(\adição_1_s5 ), .A6(\adição_1_s5 ), .B6(\adição_1_s5 ), .A7(\adição_1_s5 ), .B7(\adição_1_s5 ),
    .S0(S1), .S1(\adição_1_s1 ), .S2(\adição_1_s2 ), .S3(\adição_1_s3 ), .S4(\adição_1_s4 ),
    .S5(\adição_1_s5 ), .S6(\adição_1_s5 ), .S7(\adição_1_s5 ), .S8(\adição_1_s5 ));
  and and_9 (and_9_out, A0, B2);
  and and_10 (and_10_out, A1, B2);
  and and_11 (and_11_out, A2, B2);
  and and_12 (and_12_out, A3, B2);
  \adição  \adição_2  (
    .A0(\adição_1_s1 ), .B0(and_9_out), .A1(\adição_1_s2 ), .B1(and_10_out), .A2(\adição_1_s3 ),
    .B2(and_11_out), .A3(and_12_out), .B3(\adição_1_s4 ), .A4(\adição_1_s5 ), .B4(\adição_1_s5 ),
    .A5(\adição_1_s5 ), .B5(\adição_1_s5 ), .A6(\adição_1_s5 ), .B6(\adição_1_s5 ), .A7(\adição_1_s5 ),
    .B7(\adição_1_s5 ), .S0(S2), .S1(\adição_2_s1 ), .S2(\adição_2_s2 ), .S3(\adição_2_s3 ),
    .S4(\adição_2_s4 ), .S5(\adição_1_s5 ), .S6(\adição_1_s5 ), .S7(\adição_1_s5 ), .S8(\adição_1_s5 ));
  and and_13 (and_13_out, A0, B3);
  and and_14 (and_14_out, A1, B3);
  and and_15 (and_15_out, A2, B3);
  and and_16 (and_16_out, A3, B3);
  \adição  \adição_3  (
    .A0(\adição_2_s1 ), .B0(and_13_out), .A1(\adição_2_s2 ), .B1(and_14_out), .A2(\adição_2_s3 ),
    .B2(and_15_out), .A3(and_16_out), .B3(\adição_2_s4 ), .A4(\adição_1_s5 ), .B4(\adição_1_s5 ),
    .A5(\adição_1_s5 ), .B5(\adição_1_s5 ), .A6(\adição_1_s5 ), .B6(\adição_1_s5 ), .A7(\adição_1_s5 ),
    .B7(\adição_1_s5 ), .S0(S3), .S1(S4), .S2(S5), .S3(S6), .S4(S7), .S5(\adição_1_s5 ), .S6(\adição_1_s5 ),
    .S7(\adição_1_s5 ), .S8(\adição_1_s5 ));
  // also tied to GND on the sheet: \adição_1_s5 
endmodule
