// Digital circuit registrador.dig as structural Verilog
module registrador (
  input  CLK,
  input  L,
  input  I0,
  input  E,
  input  CLR,
  input  I1,
  input  I2,
  input  I3,
  input  I4,
  input  I5,
  input  I6,
  input  I7,
  output S0,
  output S1,
  output S2,
  output S3,
  output S4,
  output S5,
  output S6,
  output S7
);

  wire d_ff_as_1_q, d_ff_as_2_q, d_ff_as_3_q, d_ff_as_4_q, d_ff_as_5_q, d_ff_as_6_q, d_ff_as_7_q,
       d_ff_as_8_q, driver_1_out, driver_3_out, driver_5_out, driver_7_out, driver_9_out, driver_11_out,
       driver_13_out, driver_15_out;

  assign driver_1_out = E ? CLK : 1'bz;  // Driver driver_1
  D_FF_AS d_ff_as_1 (.Set(1'b0), .D(I7), .C(driver_1_out), .Clr(CLR), .Q(d_ff_as_1_q));  // open: nQ
  assign S7 = L ? d_ff_as_1_q : 1'bz;  // Driver driver_2
  assign driver_3_out = E ? CLK : 1'bz;  // Driver driver_3
  D_FF_AS d_ff_as_2 (.Set(1'b0), .D(I6), .C(driver_3_out), .Clr(CLR), .Q(d_ff_as_2_q));  // open: nQ
  assign S6 = L ? d_ff_as_2_q : 1'bz;  // Driver driver_4
  assign driver_5_out = E ? CLK : 1'bz;  // Driver driver_5
  D_FF_AS d_ff_as_3 (.Set(1'b0), .D(I5), .C(driver_5_out), .Clr(CLR), .Q(d_ff_as_3_q));  // open: nQ
  assign S5 = L ? d_ff_as_3_q : 1'bz;  // Driver driver_6
  assign driver_7_out = E ? CLK : 1'bz;  // Driver driver_7
  D_FF_AS d_ff_as_4 (.Set(1'b0), .D(I4), .C(driver_7_out), .Clr(CLR), .Q(d_ff_as_4_q));  // open: nQ
  assign S4 = L ? d_ff_as_4_q : 1'bz;  // Driver driver_8
  assign driver_9_out = E ? CLK : 1'bz;  // Driver driver_9
  D_FF_AS d_ff_as_5 (.Set(1'b0), .D(I3), .C(driver_9_out), .Clr(CLR), .Q(d_ff_as_5_q));  // open: nQ
  assign S3 = L ? d_ff_as_5_q : 1'bz;  // Driver driver_10
  assign driver_11_out = E ? CLK : 1'bz;  // Driver driver_11
  D_FF_AS d_ff_as_6 (.Set(1'b0), .D(I2), .C(driver_11_out), .Clr(CLR), .Q(d_ff_as_6_q));  // open: nQ
  assign S2 = L ? d_ff_as_6_q : 1'bz;  // Driver driver_12
  assign driver_13_out = E ? CLK : 1'bz;  // Driver driver_13
  D_FF_AS d_ff_as_7 (.Set(1'b0), .D(I1), .C(driver_13_out), .Clr(CLR), .Q(d_ff_as_7_q));  // open: nQ
  assign S1 = L ? d_ff_as_7_q : 1'bz;  // Driver driver_14
  assign driver_15_out = E ? CLK : 1'bz;  // Driver driver_15
  D_FF_AS d_ff_as_8 (.Set(1'b0), .D(I0), .C(driver_15_out), .Clr(CLR), .Q(d_ff_as_8_q));  // open: nQ
  assign S0 = L ? d_ff_as_8_q : 1'bz;  // Driver driver_16

  // Notes on the sheet:
  //   L: Ler
  //   I0: Io
  //   I1: Io
  //   I2: Io
  //   I3: Io
  //   I4: Io
  //   I5: Io
  //   I6: Io
  //   I7: Io
endmodule
