// Digital circuit subtração.dig as structural Verilog
module \subtração  (
  input  A0,
  input  B0,
  input  A1,
  input  B1,
  input  A2,
  input  B2,
  input  A3,
  input  B3,
  input  A4,
  input  B4,
  input  A5,
  input  B5,
  input  A6,
  input  B6,
  input  A7,
  input  B7,
  output S0,
  output S1,
  output S2,
  output S3,
  output S4,
  output S5,
  output S6,
  output S7,
  output S8
);

  wire \meiasubtração_1_co , \totalsubtração_2_co , \totalsubtração_3_co , \totalsubtração_4_co ,
       \totalsubtração_5_co , \totalsubtração_6_co , \totalsubtração_7_co ;

  \totalsubtração  \totalsubtração_1  (.A(A7), .B(B7), .Ci(\totalsubtração_2_co ), .S(S7), .Co(S8));
  \totalsubtração  \totalsubtração_2  (.A(A6), .B(B6), .Ci(\totalsubtração_3_co ), .S(S6), .Co(\totalsubtração_2_co ));
  \totalsubtração  \totalsubtração_3  (.A(A5), .B(B5), .Ci(\totalsubtração_4_co ), .S(S5), .Co(\totalsubtração_3_co ));
  \totalsubtração  \totalsubtração_4  (.A(A4), .B(B4), .Ci(\totalsubtração_5_co ), .S(S4), .Co(\totalsubtração_4_co ));
  \totalsubtração  \totalsubtração_5  (.A(A3), .B(B3), .Ci(\totalsubtração_6_co ), .S(S3), .Co(\totalsubtração_5_co ));
  \totalsubtração  \totalsubtração_6  (.A(A2), .B(B2), .Ci(\totalsubtração_7_co ), .S(S2), .Co(\totalsubtração_6_co ));
  \totalsubtração  \totalsubtração_7  (.A(A1), .B(B1), .Ci(\meiasubtração_1_co ), .S(S1), .Co(\totalsubtração_7_co ));
  \meiasubtração  \meiasubtração_1  (.A(A0), .B(B0), .S(S0), .Co(\meiasubtração_1_co ));
endmodule
