// Digital circuit totalcomparador.dig as structural Verilog
module totalcomparador (
  input  A,
  input  B,
  input  I_lt,
  input  I_eq,
  input  I_gt,
  output O__lt,
  output O__eq,
  output O__gt
);

  wire and_1_out, and_2_out, and_3_out, and_4_out, and_5_out, and_6_out, and_7_out, and_8_out, not_1_out,
       not_2_out;

  not not_1 (not_1_out, A);
  not not_2 (not_2_out, B);
  and and_1 (and_1_out, not_1_out, not_2_out, I_eq);
  and and_2 (and_2_out, A, B, I_eq);
  and and_3 (and_3_out, not_1_out, B);
  and and_4 (and_4_out, not_1_out, I_lt);
  and and_5 (and_5_out, B, I_lt);
  or or_1 (O__eq, and_1_out, and_2_out);
  and and_6 (and_6_out, A, not_2_out);
  and and_7 (and_7_out, not_2_out, I_gt);
  and and_8 (and_8_out, A, I_gt);
  or or_2 (O__lt, and_3_out, and_4_out, and_5_out);
  or or_3 (O__gt, and_6_out, and_7_out, and_8_out);
endmodule
