// Digital circuit totalsubtração.dig as structural Verilog
module \totalsubtração  (
  input  A,
  input  B,
  input  Ci,
  output S,
  output Co
);

  wire and_1_out, and_2_out, xor_1_out;

  xor xor_1 (xor_1_out, A, B);
  and and_1 (and_1_out, Ci, ~xor_1_out);  // And
  and and_2 (and_2_out, ~A, B);  // And
  xor xor_2 (S, xor_1_out, Ci);
  or or_1 (Co, and_1_out, and_2_out);
endmodule
