// Digital circuit ula.dig as structural Verilog
module ula (
  input  A,
  input  B,
  input  C,
  input  A0,
  input  B0,
  input  A1,
  input  B1,
  input  A2,
  input  B2,
  input  A3,
  input  B3,
  input  A4,
  input  B4,
  input  A5,
  input  B5,
  input  A6,
  input  B6,
  input  A7,
  input  B7,
  input  ESCREVER,
  input  LER
);

  wire \adição_1_s0 , \adição_1_s1 , \adição_1_s2 , \adição_1_s3 , \adição_1_s4 , \adição_1_s5 ,
       \adição_1_s6 , \adição_1_s7 , \adição_1_s8 , bits_1_s0, bits_1_s1, bits_1_s2, bits_1_s3, bits_1_s4,
       bits_1_s5, bits_1_s6, bits_1_s7, CLEAR_out, CLOCK_out, comparador_1_o__eq, comparador_1_o__gt,
       comparador_1_o__lt, diodeforward_1_out, diodeforward_3_out, diodeforward_4_out, diodeforward_5_out,
       diodeforward_6_out, diodeforward_7_out, diodeforward_8_out, diodeforward_9_out, diodeforward_10_out,
       diodeforward_11_out, diodeforward_20_out, diodeforward_22_out, driver_1_out, driver_2_out,
       driver_3_out, driver_4_out, driver_5_out, driver_6_out, driver_8_out, driver_9_out, driver_10_out,
       driver_11_out, driver_12_out, driver_13_out, driver_14_out, driver_15_out, driver_16_out,
       driver_17_out, driver_18_out, driver_19_out, driver_20_out, driver_21_out, driver_22_out,
       driver_23_out, driver_24_out, driver_25_out, driver_26_out, driver_27_out, driver_28_out,
       driver_29_out, driver_30_out, driver_31_out, driver_32_out, driver_33_out, driver_34_out,
       driver_35_out, driver_36_out, driver_37_out, driver_38_out, multiplicador_1_s0, multiplicador_1_s1,
       multiplicador_1_s2, multiplicador_1_s3, multiplicador_1_s4, multiplicador_1_s5, multiplicador_1_s6,
       multiplicador_1_s7, seletor_1_s0, seletor_1_s1, seletor_1_s2, seletor_1_s3, seletor_1_s4,
       seletor_1_s5, \subtração_1_s0 , \subtração_1_s1 , \subtração_1_s2 , \subtração_1_s3 ,
       \subtração_1_s4 , \subtração_1_s5 , \subtração_1_s6 , \subtração_1_s7 , \subtração_1_s8 ;
  wire [3:0] registrador_1_s3, registrador_1_s7;

  seletor seletor_1 (
    .A(A), .B(B), .C(C), .S0(seletor_1_s0), .S1(seletor_1_s1), .S2(seletor_1_s2), .S3(seletor_1_s3),
    .S4(seletor_1_s4), .S5(seletor_1_s5));
  Seven_Seg_Hex seven_seg_hex_1 (.d(registrador_1_s7), .dp(1'b0));
  Seven_Seg_Hex seven_seg_hex_2 (.d(registrador_1_s3), .dp(1'b0));
  DiodeForward diodeforward_1 (.in(seletor_1_s4), .out(diodeforward_1_out));
  DiodeForward diodeforward_2 (.in(seletor_1_s5), .out(diodeforward_1_out));
  PullDown pulldown_1 (.out(diodeforward_1_out));
  Button CLEAR (.out(CLEAR_out));
  Button CLOCK (.out(CLOCK_out));
  \subtração  \subtração_1  (
    .A0(A0), .B0(B0), .A1(A1), .B1(B1), .A2(A2), .B2(B2), .A3(A3), .B3(B3), .A4(A4), .B4(B4), .A5(A5),
    .B5(B5), .A6(A6), .B6(B6), .A7(A7), .B7(B7), .S0(\subtração_1_s0 ), .S1(\subtração_1_s1 ),
    .S2(\subtração_1_s2 ), .S3(\subtração_1_s3 ), .S4(\subtração_1_s4 ), .S5(\subtração_1_s5 ),
    .S6(\subtração_1_s6 ), .S7(\subtração_1_s7 ), .S8(\subtração_1_s8 ));
  \adição  \adição_1  (
    .A0(A0), .B0(B0), .A1(A1), .B1(B1), .A2(A2), .B2(B2), .A3(A3), .B3(B3), .A4(A4), .B4(B4), .A5(A5),
    .B5(B5), .A6(A6), .B6(B6), .A7(A7), .B7(B7), .S0(\adição_1_s0 ), .S1(\adição_1_s1 ), .S2(\adição_1_s2 ),
    .S3(\adição_1_s3 ), .S4(\adição_1_s4 ), .S5(\adição_1_s5 ), .S6(\adição_1_s6 ), .S7(\adição_1_s7 ),
    .S8(\adição_1_s8 ));
  comparador comparador_1 (
    .A0(A0), .B0(B0), .A1(A1), .A2(A2), .A3(A3), .A4(A4), .A5(A5), .A6(A6), .A7(A7), .B1(B1), .B2(B2),
    .B3(B3), .B4(B4), .B5(B5), .B6(B6), .B7(B7), .O__lt(comparador_1_o__lt), .O__eq(comparador_1_o__eq),
    .O__gt(comparador_1_o__gt));
  LED led_1 (.in(registrador_1_s7[3]));
  LED led_2 (.in(registrador_1_s7[2]));
  bits bits_1 (
    .I0(A0), .Shift(seletor_1_s4), .I1(A1), .I2(A2), .I3(A3), .I4(A4), .I5(A5), .I6(A6), .I7(A7),
    .S0(bits_1_s0), .S1(bits_1_s1), .S2(bits_1_s2), .S3(bits_1_s3), .S4(bits_1_s4), .S5(bits_1_s5),
    .S6(bits_1_s6), .S7(bits_1_s7));
  multiplicador multiplicador_1 (
    .A0(A0), .A1(A1), .A2(A2), .A3(A3), .B0(B0), .B1(B1), .B2(B2), .B3(B3), .S0(multiplicador_1_s0),
    .S1(multiplicador_1_s1), .S2(multiplicador_1_s2), .S3(multiplicador_1_s3), .S4(multiplicador_1_s4),
    .S5(multiplicador_1_s5), .S6(multiplicador_1_s6), .S7(multiplicador_1_s7));
  LED led_3 (.in(registrador_1_s7[1]));
  LED led_4 (.in(registrador_1_s7[0]));
  LED led_5 (.in(registrador_1_s3[3]));
  LED led_6 (.in(registrador_1_s3[2]));
  LED MAIOR (.in(diodeforward_11_out));
  LED IGUAL (.in(diodeforward_22_out));
  LED MENOR (.in(diodeforward_20_out));
  LED led_7 (.in(registrador_1_s3[1]));
  LED led_8 (.in(registrador_1_s3[0]));
  registrador registrador_1 (
    .CLK(CLOCK_out), .L(LER), .I0(diodeforward_3_out), .E(ESCREVER), .CLR(CLEAR_out),
    .I1(diodeforward_4_out), .I2(diodeforward_5_out), .I3(diodeforward_6_out), .I4(diodeforward_7_out),
    .I5(diodeforward_8_out), .I6(diodeforward_9_out), .I7(diodeforward_10_out), .S0(registrador_1_s3[0]),
    .S1(registrador_1_s3[1]), .S2(registrador_1_s3[2]), .S3(registrador_1_s3[3]), .S4(registrador_1_s7[0]),
    .S5(registrador_1_s7[1]), .S6(registrador_1_s7[2]), .S7(registrador_1_s7[3]));
  assign driver_1_out = seletor_1_s0 ? \subtração_1_s8  : 1'bz;  // Driver driver_1
  assign driver_2_out = seletor_1_s1 ? \adição_1_s8  : 1'bz;  // Driver driver_2
  assign driver_3_out = seletor_1_s0 ? \subtração_1_s7  : 1'bz;  // Driver driver_3
  assign driver_4_out = seletor_1_s1 ? \adição_1_s7  : 1'bz;  // Driver driver_4
  assign driver_5_out = diodeforward_1_out ? bits_1_s7 : 1'bz;  // Driver driver_5
  assign driver_6_out = seletor_1_s3 ? multiplicador_1_s7 : 1'bz;  // Driver driver_6
  assign driver_6_out = seletor_1_s3 ? multiplicador_1_s7 : 1'bz;  // Driver driver_7
  assign driver_8_out = seletor_1_s0 ? \subtração_1_s6  : 1'bz;  // Driver driver_8
  assign driver_9_out = seletor_1_s1 ? \adição_1_s6  : 1'bz;  // Driver driver_9
  assign driver_10_out = diodeforward_1_out ? bits_1_s6 : 1'bz;  // Driver driver_10
  assign driver_11_out = seletor_1_s3 ? multiplicador_1_s6 : 1'bz;  // Driver driver_11
  assign driver_12_out = seletor_1_s0 ? \subtração_1_s5  : 1'bz;  // Driver driver_12
  assign driver_13_out = seletor_1_s1 ? \adição_1_s5  : 1'bz;  // Driver driver_13
  assign driver_14_out = diodeforward_1_out ? bits_1_s5 : 1'bz;  // Driver driver_14
  assign driver_15_out = seletor_1_s3 ? multiplicador_1_s5 : 1'bz;  // Driver driver_15
  assign driver_16_out = seletor_1_s0 ? \subtração_1_s4  : 1'bz;  // Driver driver_16
  assign driver_17_out = seletor_1_s1 ? \adição_1_s4  : 1'bz;  // Driver driver_17
  assign driver_18_out = diodeforward_1_out ? bits_1_s4 : 1'bz;  // Driver driver_18
  assign driver_19_out = seletor_1_s3 ? multiplicador_1_s4 : 1'bz;  // Driver driver_19
  assign driver_20_out = seletor_1_s0 ? \subtração_1_s3  : 1'bz;  // Driver driver_20
  assign driver_21_out = seletor_1_s1 ? \adição_1_s3  : 1'bz;  // Driver driver_21
  assign driver_22_out = diodeforward_1_out ? bits_1_s3 : 1'bz;  // Driver driver_22
  assign driver_23_out = seletor_1_s3 ? multiplicador_1_s3 : 1'bz;  // Driver driver_23
  assign driver_24_out = seletor_1_s0 ? \subtração_1_s2  : 1'bz;  // Driver driver_24
  assign driver_25_out = seletor_1_s1 ? \adição_1_s2  : 1'bz;  // Driver driver_25
  assign driver_26_out = seletor_1_s2 ? comparador_1_o__gt : 1'bz;  // Driver driver_26
  assign driver_27_out = diodeforward_1_out ? bits_1_s2 : 1'bz;  // Driver driver_27
  assign driver_28_out = seletor_1_s3 ? multiplicador_1_s2 : 1'bz;  // Driver driver_28
  assign driver_29_out = seletor_1_s0 ? \subtração_1_s1  : 1'bz;  // Driver driver_29
  assign driver_30_out = seletor_1_s1 ? \adição_1_s1  : 1'bz;  // Driver driver_30
  assign driver_31_out = seletor_1_s2 ? comparador_1_o__eq : 1'bz;  // Driver driver_31
  assign driver_32_out = diodeforward_1_out ? bits_1_s1 : 1'bz;  // Driver driver_32
  assign driver_33_out = seletor_1_s3 ? multiplicador_1_s1 : 1'bz;  // Driver driver_33
  assign driver_34_out = seletor_1_s0 ? \subtração_1_s0  : 1'bz;  // Driver driver_34
  assign driver_35_out = seletor_1_s1 ? \adição_1_s0  : 1'bz;  // Driver driver_35
  assign driver_36_out = seletor_1_s2 ? comparador_1_o__lt : 1'bz;  // Driver driver_36
  assign driver_37_out = diodeforward_1_out ? bits_1_s0 : 1'bz;  // Driver driver_37
  assign driver_38_out = seletor_1_s3 ? multiplicador_1_s0 : 1'bz;  // Driver driver_38
  DiodeForward diodeforward_3 (.in(driver_34_out), .out(diodeforward_3_out));
  DiodeForward diodeforward_4 (.in(driver_29_out), .out(diodeforward_4_out));
  DiodeForward diodeforward_5 (.in(driver_24_out), .out(diodeforward_5_out));
  DiodeForward diodeforward_6 (.in(driver_20_out), .out(diodeforward_6_out));
  DiodeForward diodeforward_7 (.in(driver_16_out), .out(diodeforward_7_out));
  DiodeForward diodeforward_8 (.in(driver_12_out), .out(diodeforward_8_out));
  DiodeForward diodeforward_9 (.in(driver_8_out), .out(diodeforward_9_out));
  DiodeForward diodeforward_10 (.in(driver_3_out), .out(diodeforward_10_out));
  DiodeForward diodeforward_11 (.in(driver_1_out), .out(diodeforward_11_out));
  DiodeForward diodeforward_12 (.in(driver_35_out), .out(diodeforward_3_out));
  DiodeForward diodeforward_13 (.in(driver_30_out), .out(diodeforward_4_out));
  DiodeForward diodeforward_14 (.in(driver_25_out), .out(diodeforward_5_out));
  DiodeForward diodeforward_15 (.in(driver_21_out), .out(diodeforward_6_out));
  DiodeForward diodeforward_16 (.in(driver_17_out), .out(diodeforward_7_out));
  DiodeForward diodeforward_17 (.in(driver_13_out), .out(diodeforward_8_out));
  DiodeForward diodeforward_18 (.in(driver_9_out), .out(diodeforward_9_out));
  DiodeForward diodeforward_19 (.in(driver_4_out), .out(diodeforward_10_out));
  DiodeForward diodeforward_20 (.in(driver_2_out), .out(diodeforward_20_out));
  DiodeForward diodeforward_21 (.in(driver_36_out), .out(diodeforward_20_out));
  DiodeForward diodeforward_22 (.in(driver_31_out), .out(diodeforward_22_out));
  DiodeForward diodeforward_23 (.in(driver_26_out), .out(diodeforward_11_out));
  DiodeForward diodeforward_24 (.in(driver_37_out), .out(diodeforward_3_out));
  DiodeForward diodeforward_25 (.in(driver_32_out), .out(diodeforward_4_out));
  DiodeForward diodeforward_26 (.in(driver_27_out), .out(diodeforward_5_out));
  DiodeForward diodeforward_27 (.in(driver_22_out), .out(diodeforward_6_out));
  DiodeForward diodeforward_28 (.in(driver_18_out), .out(diodeforward_7_out));
  DiodeForward diodeforward_29 (.in(driver_14_out), .out(diodeforward_8_out));
  DiodeForward diodeforward_30 (.in(driver_10_out), .out(diodeforward_9_out));
  DiodeForward diodeforward_31 (.in(driver_5_out), .out(diodeforward_10_out));
  DiodeForward diodeforward_32 (.in(driver_38_out), .out(diodeforward_3_out));
  DiodeForward diodeforward_33 (.in(driver_33_out), .out(diodeforward_4_out));
  DiodeForward diodeforward_34 (.in(driver_28_out), .out(diodeforward_5_out));
  DiodeForward diodeforward_35 (.in(driver_23_out), .out(diodeforward_6_out));
  DiodeForward diodeforward_36 (.in(driver_19_out), .out(diodeforward_7_out));
  DiodeForward diodeforward_37 (.in(driver_15_out), .out(diodeforward_8_out));
  DiodeForward diodeforward_38 (.in(driver_11_out), .out(diodeforward_9_out));
  DiodeForward diodeforward_39 (.in(driver_6_out), .out(diodeforward_10_out));
  PullDown pulldown_2 (.out(diodeforward_20_out));
  PullDown pulldown_3 (.out(diodeforward_22_out));
  PullDown pulldown_4 (.out(diodeforward_11_out));
  PullDown pulldown_5 (.out(diodeforward_10_out));
  PullDown pulldown_6 (.out(diodeforward_9_out));
  PullDown pulldown_7 (.out(diodeforward_8_out));
  PullDown pulldown_8 (.out(diodeforward_7_out));
  PullDown pulldown_9 (.out(diodeforward_6_out));
  PullDown pulldown_10 (.out(diodeforward_5_out));
  PullDown pulldown_11 (.out(diodeforward_4_out));
  PullDown pulldown_12 (.out(diodeforward_3_out));
  PullDown pulldown_13 ();  // open: out

  // Notes on the sheet:
  //   000 - Subtração
  //   001 - Adição
  //   010 - Comparação
  //   011 - Multiplicação
  //   100 - Shift para a Direita
  //   101 - Shift para a esquerda
endmodule
